# Fritzing sketch instument di wang (saved by Fritzing 0.9.3b)
circuit board: 8.46667cm x 5.64444cm
breadboards: 1

parts:
  hc-sr1 = hc-sr04
  Part1 = Arduino Uno (Rev3)
  R1 = Rotary Potentiometer (Large) [maximum_resistance=100kΩ package=THT]

nets (from the schematic view):
  VCC: hc-sr1.VCC, Part1.5V, R1.leg2
  N1: hc-sr1.Trig, Part1.D10_PWM/SS
  N2: hc-sr1.Echo, Part1.D11_PWM/MOSI
  GND: hc-sr1.GND, Part1.GND, R1.leg1
  N3: Part1.A0, R1.wiper
